# Fritzing sketch XCSensorSketch (saved by Fritzing 0.8.5b)
circuit board: 8.46667cm x 5.64444cm
breadboards: 1

parts:
  Part1 = Arduino Pro Mini 328 - 3.3 V/8MHz
  GY1 = MPU-6050 Board GY-521 [form="♀ (female)" package=THT]
  Part2 = HMC5883L Triple-axis Magnetometer [part_number=1746]
  Part3 = Bluetooth HC-05
  U1 = ESP8266 ESP-01 Upgraded WiFi Module [part_number=ESP8266]
  Part4 = KY-015 Temperature & Humidity Sensor Module [package="Breakout board"]
  Part5 = Assembled uBLOX MAX-6 Pico Breakout with Chip Scale Antenna
  Part6 = MS5611
  Part7 = MS5611

nets:
  N1: Part1.D0/TX, Part5.RXD
  N2: Part1.D1/RX, Part5.TXD
  N3: Part1.A4, GY1.pin4, Part2.SDA, Part6.SDA
  N4: Part1.A5, Part2.SCL, Part6.SCL
  N5: Part1.D8, Part3.RXD
  N6: Part1.D7, Part3.TXD
  N7: Part1.D5_PWM, Part4.S
  N8: Part1.D3_PWM, U1.TXD
  N9: Part1.D2, U1.RXD
  +5V: GY1.pin1, Part4.Vin, Part6.+5V, Part7.+5V
  GND: GY1.pin2, Part4.-, Part6.GND, Part7.GND
  GND_2: Part3.GND, U1.GND, Part5.GND
  VCC: Part3.VCC, U1.VCC, U1.CH_PD, Part5.VCC

custom parts:
  Arduino Pro Mini 328 - 3.3 V/8MHz: Versión de Arduino Pro Mini basada en MEGA328P a 8MHz y alimentada a 3.3 voltios.
  MPU-6050 Board GY-521: Acelerometro y Giroscopio MPU-6050 Board GY-521
  HMC5883L Triple-axis Magnetometer: A magnetometer can sense where the strongest magnetic force is coming from, generally used to detect magnetic north. We based this breakout on a popular and well loved magnetometer, the HMC5883L. This compact sensor uses I2C to communicate and its very easy to use. Since it's a 3.3V max chip, we added circuitry to make it 5V-safe logic and power, for easy use with either 3 or 5V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
  ESP8266 ESP-01 Upgraded WiFi Module: Upgraded Version ESP-01,all Flash are upgraded to 1M byte.Also support Cloud service remote transmission.
  KY-015 Temperature & Humidity Sensor Module: KY-015 temperature and humidity sensor module, provides a low-latency serial interface to measure humidity and temperature.
  Assembled uBLOX MAX-6 Pico Breakout with Chip Scale Antenna: The board is assembled with a uBLOX MAX-6 module, chip scale antenna and a decoupling capacitor. This board has VCC, GND and RX & TX, SCL & SDA for I2C. MAX comes in an ultra-compact, easy-to-mount 9.7mm x 10.1mm LCC package, and supports temperatures down to -40'C. Supports temperatures down to -40'C UART interface. RTC crystal for faster warm and hot starts Suitable for HAB Usage Max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
  MS5611: This precision sensor from Bosch is the best low-cost sensing solution for measuring barometric pressure and temperature. Because pressure changes with altitude you can also use it as an altimeter! The sensor is soldered onto a PCB with a 3.3V regulator, I2C level shifter and pull-up resistors on the I2C pins. The BMP180 is the next-generation of sensors from Bosch, and replaces the BMP085.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
